// Logisim project logisim.circ as structural Verilog: 14 circuits, main circuit main
module main (
);

  wire alu_1_carry;
  wire [7:0] alu_1_accumulator_2, undriven;

  ALU alu_1 (
    .Accumulator(alu_1_accumulator_2), .BUS(undriven), .Carry(alu_1_carry),
    .Accumulator_2(alu_1_accumulator_2));  // open: Active, Control_Unit
  LED led_1 (.in(alu_1_accumulator_2[0]));
  LED led_2 (.in(alu_1_accumulator_2[1]));
  LED led_3 (.in(alu_1_accumulator_2[2]));
  LED led_4 (.in(alu_1_accumulator_2[3]));
  LED led_5 (.in(alu_1_accumulator_2[4]));
  LED led_6 (.in(alu_1_accumulator_2[5]));
  LED led_7 (.in(alu_1_accumulator_2[6]));
  LED led_8 (.in(alu_1_accumulator_2[7]));
  LED Carry (.in(alu_1_carry));
  LED led_9 (.in(undriven[0]));
  LED led_10 (.in(undriven[1]));
  LED led_11 (.in(undriven[2]));
  LED led_12 (.in(undriven[3]));
  LED led_13 (.in(undriven[4]));
  LED led_14 (.in(undriven[5]));
  LED led_15 (.in(undriven[6]));
  LED led_16 (.in(undriven[7]));
endmodule

module ALU (
  input  [7:0] Accumulator,
  input  [7:0] BUS,
  input  Active,
  input  [2:0] Control_Unit,
  output Carry,
  output [7:0] Accumulator_2
);

  wire Adder_carry;
  wire [7:0] Adder_output, And_output_and, Inverter_output, multiplexer_1_out, Or_output_acc, shl_output_acc,
       shr_output_acc, Xor_output_acc;

  And And (.Input_Acc(Accumulator), .Input_Bus(BUS), .Output_AND(And_output_and));
  Or Or (.Input_Acc(Accumulator), .Input_Bus(BUS), .Output_Acc(Or_output_acc));
  Xor Xor (.Input_Acc(Accumulator), .Input_Bus(BUS), .Output_Acc(Xor_output_acc));
  shl shl (.Input_Acc(Accumulator), .Output_Acc(shl_output_acc), .Input_Bus(BUS));
  shr shr (.Input_Acc(Accumulator), .Output_Acc(shr_output_acc), .Input_Bus(BUS));
  Adder Adder (.Sub(Control_Unit[0]), .A(Accumulator), .B(BUS), .Output(Adder_output), .Carry(Adder_carry));
  Inverter Inverter (.Input(Accumulator), .Output(Inverter_output));
  Multiplexer #(.select(3), .width(8), .enable("false")) multiplexer_1 (
    .in0(Adder_output), .in1(Adder_output), .in2(And_output_and), .in3(Or_output_acc), .in4(Xor_output_acc),
    .in5(Inverter_output), .in6(shl_output_acc), .in7(shr_output_acc), .out(multiplexer_1_out),
    .sel(Control_Unit));
  and and_2 (Carry, Adder_carry, ~Control_Unit[2], ~Control_Unit[1]);  // AND_Gate
  assign Accumulator_2 = Active ? multiplexer_1_out : 8'bz;  // Controlled_Buffer controlled_buffer_1
endmodule

module Inverter (
  input  [7:0] Input,
  output [7:0] Output
);

  assign Output = ~Input;  // NOT_Gate not_1, 8 bits wide
endmodule

module Adder (
  input  Sub,
  input  [7:0] A,
  input  [7:0] B,
  output [7:0] Output,
  output Carry
);

  wire fulladder_1_carry_out, fulladder_2_carry_out, fulladder_3_carry_out, fulladder_4_carry_out,
       fulladder_5_carry_out, fulladder_6_carry_out, fulladder_7_carry_out, fulladder_8_carry_out, xor_1_out,
       xor_2_out, xor_3_out, xor_4_out, xor_5_out, xor_6_out, xor_7_out, xor_8_out;

  xor xor_1 (xor_1_out, B[0], Sub);
  xor xor_2 (xor_2_out, B[1], Sub);
  xor xor_3 (xor_3_out, B[2], Sub);
  xor xor_4 (xor_4_out, B[3], Sub);
  xor xor_5 (xor_5_out, B[4], Sub);
  xor xor_6 (xor_6_out, B[5], Sub);
  xor xor_7 (xor_7_out, B[6], Sub);
  xor xor_8 (xor_8_out, B[7], Sub);
  FullAdder fulladder_1 (.Carry_In(Sub), .A(A[0]), .B(xor_1_out), .Sum(Output[0]), .Carry_Out(fulladder_1_carry_out));
  FullAdder fulladder_2 (
    .Carry_In(fulladder_1_carry_out), .A(A[1]), .B(xor_2_out), .Sum(Output[1]),
    .Carry_Out(fulladder_2_carry_out));
  FullAdder fulladder_3 (
    .Carry_In(fulladder_2_carry_out), .A(A[2]), .B(xor_3_out), .Sum(Output[2]),
    .Carry_Out(fulladder_3_carry_out));
  FullAdder fulladder_4 (
    .Carry_In(fulladder_3_carry_out), .A(A[3]), .B(xor_4_out), .Sum(Output[3]),
    .Carry_Out(fulladder_4_carry_out));
  FullAdder fulladder_5 (
    .Carry_In(fulladder_4_carry_out), .A(A[4]), .B(xor_5_out), .Sum(Output[4]),
    .Carry_Out(fulladder_5_carry_out));
  FullAdder fulladder_6 (
    .Carry_In(fulladder_5_carry_out), .A(A[5]), .B(xor_6_out), .Sum(Output[5]),
    .Carry_Out(fulladder_6_carry_out));
  FullAdder fulladder_7 (
    .Carry_In(fulladder_6_carry_out), .A(A[6]), .B(xor_7_out), .Sum(Output[6]),
    .Carry_Out(fulladder_7_carry_out));
  FullAdder fulladder_8 (
    .Carry_In(fulladder_7_carry_out), .A(A[7]), .B(xor_8_out), .Sum(Output[7]),
    .Carry_Out(fulladder_8_carry_out));
  xor xor_9 (Carry, fulladder_8_carry_out, Sub);
endmodule

module FullAdder (
  input  Carry_In,
  input  A,
  input  B,
  output Sum,
  output Carry_Out
);

  wire halfadder_1_carry, halfadder_1_sum, halfadder_2_carry;

  HalfAdder halfadder_1 (.A(A), .B(B), .Sum(halfadder_1_sum), .Carry(halfadder_1_carry));
  HalfAdder halfadder_2 (.A(Carry_In), .B(halfadder_1_sum), .Sum(Sum), .Carry(halfadder_2_carry));
  or or_1 (Carry_Out, halfadder_2_carry, halfadder_1_carry);
endmodule

module HalfAdder (
  input  A,
  input  B,
  output Sum,
  output Carry
);

  xor xor_1 (Sum, A, B);
  and and_1 (Carry, A, B);
endmodule

module And (
  input  [7:0] Input_Acc,
  input  [7:0] Input_Bus,
  output [7:0] Output_AND
);

  assign Output_AND = Input_Acc & Input_Bus;  // AND_Gate and_1, 8 bits wide
endmodule

module Or (
  input  [7:0] Input_Acc,
  input  [7:0] Input_Bus,
  output [7:0] Output_Acc
);

  assign Output_Acc = Input_Acc | Input_Bus;  // OR_Gate or_1, 8 bits wide
endmodule

module Xor (
  input  [7:0] Input_Acc,
  input  [7:0] Input_Bus,
  output [7:0] Output_Acc
);

  assign Output_Acc = Input_Acc ^ Input_Bus;  // XOR_Gate xor_1, 8 bits wide
endmodule

module shl (
  input  [7:0] Input_Acc,
  input  [7:0] Input_Bus,
  output [7:0] Output_Acc
);

  wire [7:0] multiplexer_8_out;

  Multiplexer #(.select(3), .enable("false")) multiplexer_1 (
    .in0(Input_Acc[0]), .in1(1'b0), .in2(1'b0), .in3(1'b0), .in4(1'b0), .in5(1'b0), .in6(1'b0), .in7(1'b0),
    .out(multiplexer_8_out[7]), .sel(Input_Bus[2:0]));
  Multiplexer #(.select(3), .enable("false")) multiplexer_2 (
    .in0(Input_Acc[2]), .in1(Input_Acc[1]), .in2(Input_Acc[0]), .in3(1'b0), .in4(1'b0), .in5(1'b0),
    .in6(1'b0), .in7(1'b0), .out(multiplexer_8_out[5]), .sel(Input_Bus[2:0]));
  Multiplexer #(.select(3), .enable("false")) multiplexer_3 (
    .in0(Input_Acc[1]), .in1(Input_Acc[0]), .in2(1'b0), .in3(1'b0), .in4(1'b0), .in5(1'b0), .in6(1'b0),
    .in7(1'b0), .out(multiplexer_8_out[6]), .sel(Input_Bus[2:0]));
  Multiplexer #(.select(3), .enable("false")) multiplexer_4 (
    .in0(Input_Acc[3]), .in1(Input_Acc[2]), .in2(Input_Acc[1]), .in3(Input_Acc[0]), .in4(1'b0), .in5(1'b0),
    .in6(1'b0), .in7(1'b0), .out(multiplexer_8_out[4]), .sel(Input_Bus[2:0]));
  Multiplexer #(.select(3), .enable("false")) multiplexer_5 (
    .in0(Input_Acc[4]), .in1(Input_Acc[3]), .in2(Input_Acc[2]), .in3(Input_Acc[1]), .in4(Input_Acc[0]),
    .in5(1'b0), .in6(1'b0), .in7(1'b0), .out(multiplexer_8_out[3]), .sel(Input_Bus[2:0]));
  Multiplexer #(.select(3), .enable("false")) multiplexer_6 (
    .in0(Input_Acc[5]), .in1(Input_Acc[4]), .in2(Input_Acc[3]), .in3(Input_Acc[2]), .in4(Input_Acc[1]),
    .in5(Input_Acc[0]), .in6(1'b0), .in7(1'b0), .out(multiplexer_8_out[2]), .sel(Input_Bus[2:0]));
  Multiplexer #(.select(3), .enable("false")) multiplexer_7 (
    .in0(Input_Acc[6]), .in1(Input_Acc[5]), .in2(Input_Acc[4]), .in3(Input_Acc[3]), .in4(Input_Acc[2]),
    .in5(Input_Acc[1]), .in6(Input_Acc[0]), .in7(1'b0), .out(multiplexer_8_out[1]), .sel(Input_Bus[2:0]));
  Multiplexer #(.select(3), .enable("false")) multiplexer_8 (
    .in0(Input_Acc[7]), .in1(Input_Acc[6]), .in2(Input_Acc[5]), .in3(Input_Acc[4]), .in4(Input_Acc[3]),
    .in5(Input_Acc[2]), .in6(Input_Acc[1]), .in7(Input_Acc[0]), .out(multiplexer_8_out[0]),
    .sel(Input_Bus[2:0]));
  assign Output_Acc = Input_Bus[3] ? multiplexer_8_out : 8'bz;  // Controlled_Buffer controlled_buffer_1
endmodule

module shr (
  input  [7:0] Input_Acc,
  input  [7:0] Input_Bus,
  output [7:0] Output_Acc
);

  wire [7:0] multiplexer_8_out;

  Multiplexer #(.select(3), .enable("false")) multiplexer_1 (
    .in0(Input_Acc[7]), .in1(Input_Acc[7]), .in2(Input_Acc[7]), .in3(Input_Acc[7]), .in4(Input_Acc[7]),
    .in5(Input_Acc[7]), .in6(Input_Acc[7]), .in7(Input_Acc[7]), .out(multiplexer_8_out[7]),
    .sel(Input_Bus[2:0]));
  Multiplexer #(.select(3), .enable("false")) multiplexer_2 (
    .in0(Input_Acc[5]), .in1(Input_Acc[6]), .in2(Input_Acc[7]), .in3(Input_Acc[7]), .in4(Input_Acc[7]),
    .in5(Input_Acc[7]), .in6(Input_Acc[7]), .in7(Input_Acc[7]), .out(multiplexer_8_out[5]),
    .sel(Input_Bus[2:0]));
  Multiplexer #(.select(3), .enable("false")) multiplexer_3 (
    .in0(Input_Acc[6]), .in1(Input_Acc[7]), .in2(Input_Acc[7]), .in3(Input_Acc[7]), .in4(Input_Acc[7]),
    .in5(Input_Acc[7]), .in6(Input_Acc[7]), .in7(Input_Acc[7]), .out(multiplexer_8_out[6]),
    .sel(Input_Bus[2:0]));
  Multiplexer #(.select(3), .enable("false")) multiplexer_4 (
    .in0(Input_Acc[4]), .in1(Input_Acc[5]), .in2(Input_Acc[6]), .in3(Input_Acc[7]), .in4(Input_Acc[7]),
    .in5(Input_Acc[7]), .in6(Input_Acc[7]), .in7(Input_Acc[7]), .out(multiplexer_8_out[4]),
    .sel(Input_Bus[2:0]));
  Multiplexer #(.select(3), .enable("false")) multiplexer_5 (
    .in0(Input_Acc[3]), .in1(Input_Acc[4]), .in2(Input_Acc[5]), .in3(Input_Acc[6]), .in4(Input_Acc[7]),
    .in5(Input_Acc[7]), .in6(Input_Acc[7]), .in7(Input_Acc[7]), .out(multiplexer_8_out[3]),
    .sel(Input_Bus[2:0]));
  Multiplexer #(.select(3), .enable("false")) multiplexer_6 (
    .in0(Input_Acc[2]), .in1(Input_Acc[3]), .in2(Input_Acc[4]), .in3(Input_Acc[5]), .in4(Input_Acc[6]),
    .in5(Input_Acc[7]), .in6(Input_Acc[7]), .in7(Input_Acc[7]), .out(multiplexer_8_out[2]),
    .sel(Input_Bus[2:0]));
  Multiplexer #(.select(3), .enable("false")) multiplexer_7 (
    .in0(Input_Acc[1]), .in1(Input_Acc[2]), .in2(Input_Acc[3]), .in3(Input_Acc[4]), .in4(Input_Acc[5]),
    .in5(Input_Acc[6]), .in6(Input_Acc[7]), .in7(Input_Acc[7]), .out(multiplexer_8_out[1]),
    .sel(Input_Bus[2:0]));
  Multiplexer #(.select(3), .enable("false")) multiplexer_8 (
    .in0(Input_Acc[0]), .in1(Input_Acc[1]), .in2(Input_Acc[2]), .in3(Input_Acc[3]), .in4(Input_Acc[4]),
    .in5(Input_Acc[5]), .in6(Input_Acc[6]), .in7(Input_Acc[7]), .out(multiplexer_8_out[0]),
    .sel(Input_Bus[2:0]));
  assign Output_Acc = Input_Bus[3] ? multiplexer_8_out : 8'bz;  // Controlled_Buffer controlled_buffer_1
endmodule

module RS_getaktet (
  input  Set,
  input  Clock,
  input  Reset,
  output Out,
  output Out_negate
);

  wire nand_1_out, nand_2_out;

  nand nand_1 (nand_1_out, Set, Clock);
  nand nand_2 (nand_2_out, Clock, Reset);
  nand nand_3 (Out, nand_1_out, Out_negate);
  nand nand_4 (Out_negate, Out, nand_2_out);
endmodule

module Tests (
  input  Sub,
  input  [7:0] A,
  input  [7:0] B,
  input  [7:0] in_4,
  input  [7:0] in_5,
  output [7:0] out_6,
  output [7:0] out_7,
  output out_8,
  output [7:0] out_9,
  output [7:0] out_10
);

  Or or_1 (.Input_Acc(in_5), .Input_Bus(in_4), .Output_Acc(out_10));
  Inverter inverter_1 (.Input(8'hfe), .Output(out_6));
  Adder adder_1 (.Sub(Sub), .A(A), .B(B), .Output(out_7), .Carry(out_8));
  Xor xor_1 (.Input_Acc(in_4), .Input_Bus(in_5), .Output_Acc(out_9));
endmodule

module RS_ungetaktet (
  input  Out,
  input  R,
  input  S,
  input  Out_negate
);

  nor nor_1 (Out, Out_negate, R);
  nor nor_2 (Out_negate, S, Out);
endmodule
