// Logisim project logisim74.circ as structural Verilog
module ALU74 (
  input  [7:0] Accu,
  input  [7:0] Bus,
  input  in_3,
  input  [3:0] CU,
  output Garry,
  output [7:0] Accu_2
);

  wire [7:0] ADD_summe, AND_out_3, bit_extender_1_out, INV_output, MUX_2_IN_2_p17, MUX_2_IN_4_p19, OR_out_3,
       SHL_output_acc, SHR_output_acc, XOR_out_3;

  // DIP_74157 MUX_2_IN: pin names not known; wires that end beside it: CU[0], 1'b0, Bus[4], Bus[3], Accu[4], Accu[3], MUX_2_IN_2_p17[4], MUX_2_IN_2_p17[3], Bus[5], Bus[2], Accu[5]
  // DIP_74157 MUX_2_IN_2: pin names not known; wires that end beside it: Accu[2], MUX_2_IN_2_p17[5], MUX_2_IN_2_p17[2], CU[0], 1'b0, Accu[6], Bus[1], Bus[6], Accu[1], MUX_2_IN_2_p17[6], MUX_2_IN_2_p17[1], Bus[7], Bus[0], Accu[7], Accu[0], MUX_2_IN_2_p17[7], MUX_2_IN_2_p17[0]
  assign bit_extender_1_out = {{7{1'b0}}, 1'b0};  // Bit_Extender bit_extender_1
  // DIP_74157 MUX_2_IN_3: pin names not known; wires that end beside it: CU[0], 1'b0, Accu[4], Accu[3], Bus[4], Bus[3], MUX_2_IN_4_p19[4], MUX_2_IN_4_p19[3], Accu[5]
  // DIP_74157 MUX_2_IN_4: pin names not known; wires that end beside it: Accu[2], Bus[5], Bus[2], MUX_2_IN_4_p19[5], MUX_2_IN_4_p19[2], CU[0], 1'b0, Accu[6], Accu[1], Bus[6], Bus[1], MUX_2_IN_4_p19[6], MUX_2_IN_4_p19[1], Accu[7], Accu[0], Bus[7], Bus[0], MUX_2_IN_4_p19[7], MUX_2_IN_4_p19[0]
  AND74 AND (.Accu(MUX_2_IN_4_p19), .Bus(MUX_2_IN_2_p17), .out_3(AND_out_3));
  OR74 OR (.Accu(MUX_2_IN_4_p19), .Bus(MUX_2_IN_2_p17), .out_3(OR_out_3));
  XOR74 XOR (.Accu(MUX_2_IN_4_p19), .Bus(MUX_2_IN_2_p17), .out_3(XOR_out_3));
  ADD74 ADD (.SUB(CU[2]), .Bus(MUX_2_IN_2_p17), .SUMME(ADD_summe), .CARRY(Garry), .Accu(MUX_2_IN_4_p19));
  SHL74 SHL (.Bus(MUX_2_IN_2_p17), .Accu(MUX_2_IN_4_p19), .Output_Acc(SHL_output_acc));
  SHR74 SHR (.Bus(MUX_2_IN_2_p17), .Accu(MUX_2_IN_4_p19), .Output_Acc(SHR_output_acc));
  INV74 INV (.Input(MUX_2_IN_4_p19), .Output(INV_output));
  MUX mux_1 (
    .AND(AND_out_3), .OR(OR_out_3), .XOR(XOR_out_3), .ADD1(ADD_summe), .ADD2(ADD_summe), .ADD3(ADD_summe),
    .ZERO1(bit_extender_1_out), .ZERO2(bit_extender_1_out), .SHL1(SHL_output_acc), .SHL2(SHL_output_acc),
    .SHR1(SHR_output_acc), .SHR2(SHR_output_acc), .ACCU1(MUX_2_IN_4_p19), .ACCU2(MUX_2_IN_4_p19),
    .INV1(INV_output), .INV2(INV_output), .Output_Accu(Accu_2), .CU(CU));
  CMPZERO74 CMPZERO (.Input(Accu_2), .is_zero(in_3));
endmodule

module AND74 (
  input  [7:0] Accu,
  input  [7:0] Bus,
  output [7:0] out_3
);

  // DIP_7408 AND: pin names not known; wires that end beside it: Bus[7], Bus[3], Accu[7], Accu[3], out_3[7], out_3[3], Bus[6], Bus[2], Accu[6]
  // DIP_7408 AND_2: pin names not known; wires that end beside it: Accu[2], out_3[6], out_3[2], Bus[5], Bus[1], Accu[5], Accu[1], out_3[5], out_3[1], Bus[4], Bus[0], Accu[4], Accu[0], out_3[4], out_3[0]
endmodule

module OR74 (
  input  [7:0] Accu,
  input  [7:0] Bus,
  output [7:0] out_3
);

  // DIP_7432 OR: pin names not known; wires that end beside it: Bus[7], Bus[3], Accu[7], Accu[3], out_3[7], out_3[3], Bus[6], Bus[2], Accu[6]
  // DIP_7432 OR_2: pin names not known; wires that end beside it: Accu[2], out_3[6], out_3[2], Bus[5], Bus[1], Accu[5], Accu[1], out_3[5], out_3[1], Bus[4], Bus[0], Accu[4], Accu[0], out_3[4], out_3[0]
endmodule

module XOR74 (
  input  [7:0] Accu,
  input  [7:0] Bus,
  output [7:0] out_3
);

  // DIP_7486 XOR: pin names not known; wires that end beside it: Bus[7], Bus[3], Accu[7], Accu[3], out_3[7], out_3[3], Bus[6], Bus[2], Accu[6]
  // DIP_7486 XOR_2: pin names not known; wires that end beside it: Accu[2], out_3[6], out_3[2], Bus[5], Bus[1], Accu[5], Accu[1], out_3[5], out_3[1], Bus[4], Bus[0], Accu[4], Accu[0], out_3[4], out_3[0]
endmodule

module ADD74 (
  input  [7:0] Bus,
  input  SUB,
  input  [7:0] Accu,
  output [7:0] SUMME,
  output CARRY
);

  wire AND_2_p2, AND_2_p3, AND_2_p4, AND_2_p8, AND_2_p9, AND_2_p10, AND_3_p2, AND_3_p3, AND_3_p8, AND_3_p9,
       AND_4_p2, AND_4_p3, AND_4_p8, AND_4_p9, AND_4_p14, AND_4_p15, AND_p1, AND_p5, AND_p6, AND_p7, OR_p5,
       XOR_2_p2, XOR_2_p3, XOR_2_p6, XOR_2_p8, XOR_2_p9, XOR_2_p12, XOR_3_p2, XOR_3_p3, XOR_3_p8, XOR_4_p2,
       XOR_4_p8, XOR_4_p14, XOR_5_p3, XOR_5_p9, XOR_6_p6, XOR_p3, XOR_p5, XOR_p6, XOR_p9;

  // DIP_7486 XOR: pin names not known; wires that end beside it: Accu[0], SUB, XOR_p3, Bus[7], XOR_p5, XOR_p6, Accu[1], SUB, XOR_p9
  // DIP_7486 XOR_2: pin names not known; wires that end beside it: Bus[6], XOR_2_p2, XOR_2_p3, Accu[2], SUB, XOR_2_p6, Bus[5], XOR_2_p8, XOR_2_p9, Accu[3], SUB, XOR_2_p12
  // DIP_7486 XOR_3: pin names not known; wires that end beside it: Bus[4], XOR_3_p2, XOR_3_p3, Accu[4], SUB, XOR_3_p3, Bus[3], XOR_3_p8, XOR_2_p12, Accu[5], SUB, XOR_2_p9
  // DIP_7486 XOR_4: pin names not known; wires that end beside it: Bus[2], XOR_4_p2, XOR_2_p6, Accu[6], SUB, XOR_2_p3, Bus[1], XOR_4_p8, XOR_p9, XOR_p6, SUB, Accu[7], Bus[0], XOR_4_p14, XOR_p3
  // DIP_7408 AND: pin names not known; wires that end beside it: AND_p1, Accu[7], XOR_4_p14, XOR_p6, AND_p5, AND_p6, AND_p7, Accu[6], XOR_4_p8
  // DIP_7486 XOR_5: pin names not known; wires that end beside it: XOR_3_p2, XOR_3_p8, XOR_5_p3, AND_p1, SUMME[3], SUMME[4], XOR_2_p8, XOR_4_p2, XOR_5_p9
  // DIP_7408 AND_2: pin names not known; wires that end beside it: XOR_2_p3, AND_2_p2, AND_2_p3, AND_2_p4, Accu[5], XOR_4_p2, XOR_2_p9, AND_2_p8, AND_2_p9, AND_2_p10, Accu[4], XOR_3_p8
  // DIP_7486 XOR_6: pin names not known; wires that end beside it: AND_p7, SUMME[2], SUMME[5], XOR_2_p2, XOR_4_p8, XOR_6_p6, AND_2_p4, SUMME[1], SUMME[6], XOR_p5, XOR_4_p14, SUB, AND_2_p10, SUMME[0], SUMME[7]
  // DIP_7408 AND_3: pin names not known; wires that end beside it: XOR_3_p3, AND_3_p2, AND_3_p3, XOR_5_p3, Accu[3], XOR_3_p2, XOR_2_p12, AND_3_p8, AND_3_p9, XOR_5_p9, Accu[2], XOR_2_p8
  // DIP_7408 AND_4: pin names not known; wires that end beside it: XOR_2_p6, AND_4_p2, AND_4_p3, XOR_6_p6, Accu[1], XOR_2_p2, XOR_p9, AND_4_p8, AND_4_p9, SUB, Accu[0], XOR_p5, XOR_p3, AND_4_p14, AND_4_p15
  // DIP_7432 OR: pin names not known; wires that end beside it: AND_p5, AND_3_p8, AND_p6, AND_3_p9, OR_p5, AND_2_p10, AND_2_p2, AND_4_p2, AND_2_p3
  // DIP_7432 OR_2: pin names not known; wires that end beside it: AND_4_p3, AND_p1, XOR_5_p3, AND_2_p8, AND_4_p8, AND_2_p9, AND_4_p9, AND_p7, XOR_5_p9, AND_3_p2, AND_4_p14, AND_3_p3, AND_4_p15, AND_2_p4, XOR_6_p6
  // DIP_7486 XOR_7: pin names not known; wires that end beside it: OR_p5, SUB, CARRY
endmodule

module SHL74 (
  input  [7:0] Accu,
  input  [7:0] Bus,
  output [7:0] Output_Acc
);

  wire AND_2_p6, AND_2_p7, AND_2_p12, AND_2_p13, AND_p3, AND_p9, MUX_8_in_2_p5, MUX_8_in_p5, NOT_p3, OR_p3,
       OR_p4, OR_p5, OR_p6;

  // DIP_7432 OR: pin names not known; wires that end beside it: Bus[7], Bus[5], OR_p3, OR_p4, OR_p5, OR_p6, Bus[6], Bus[4], OR_p6, Bus[3], OR_p4
  // DIP_7404 NOT: pin names not known; wires that end beside it: OR_p3, OR_p5, NOT_p3
  // DIP_74151 MUX_8_in: pin names not known; wires that end beside it: 1'b0, 1'b0, 1'b0, Accu[0], MUX_8_in_p5, 1'b0, 1'b0, 1'b0, 1'b0, 1'b0, Bus[0], Bus[1], Bus[2]
  // DIP_7408 AND: pin names not known; wires that end beside it: NOT_p3, NOT_p3, AND_p3, MUX_8_in_p5, Output_Acc[4], Output_Acc[0], NOT_p3, NOT_p3, AND_p9
  // DIP_74151 MUX_8_in_2: pin names not known; wires that end beside it: 1'b0, 1'b0, Accu[0], Accu[1], MUX_8_in_2_p5, 1'b0, 1'b0, 1'b0, 1'b0, 1'b0, Bus[0], Bus[1], Bus[2]
  // DIP_7408 AND_2: pin names not known; wires that end beside it: MUX_8_in_2_p5, Output_Acc[5], Output_Acc[1], NOT_p3, NOT_p3, AND_2_p6, AND_2_p7, Output_Acc[6], Output_Acc[2], NOT_p3, NOT_p3, AND_2_p12, AND_2_p13, Output_Acc[7], Output_Acc[3]
  // DIP_74151 MUX_8_in_3: pin names not known; wires that end beside it: 1'b0, Accu[0], Accu[1], Accu[2], AND_2_p7, 1'b0, 1'b0, 1'b0, 1'b0, 1'b0, Bus[0], Bus[1], Bus[2]
  // DIP_74151 MUX_8_in_4: pin names not known; wires that end beside it: Accu[0], Accu[1], Accu[2], Accu[3], AND_2_p13, 1'b0, 1'b0, 1'b0, 1'b0, 1'b0, Bus[0], Bus[1], Bus[2]
  // DIP_74151 MUX_8_in_5: pin names not known; wires that end beside it: Accu[1], Accu[2], Accu[3], Accu[4], AND_p3, 1'b0, Accu[0], 1'b0, 1'b0, 1'b0, Bus[0], Bus[1], Bus[2]
  // DIP_74151 MUX_8_in_6: pin names not known; wires that end beside it: Accu[2], Accu[3], Accu[4], Accu[5], AND_p9, 1'b0, Accu[1], Accu[0], 1'b0, 1'b0, Bus[0], Bus[1], Bus[2]
  // DIP_74151 MUX_8_in_7: pin names not known; wires that end beside it: Accu[3], Accu[4], Accu[5], Accu[6], AND_2_p6, 1'b0, Accu[2], Accu[1], Accu[0], 1'b0, Bus[0], Bus[1], Bus[2]
  // DIP_74151 MUX_8_in_8: pin names not known; wires that end beside it: Accu[4], Accu[5], Accu[6], Accu[7], AND_2_p12, 1'b0, Accu[3], Accu[2], Accu[1], Accu[0], Bus[0], Bus[1], Bus[2]
endmodule

module SHR74 (
  input  [7:0] Accu,
  input  [7:0] Bus,
  output [7:0] Output_Acc
);

  wire AND_2_p6, AND_2_p7, AND_2_p12, AND_2_p13, AND_p3, AND_p9, MUX_8_in_2_p5, MUX_8_in_p5, NOT_p3, OR_p3,
       OR_p4, OR_p5, OR_p6;

  // DIP_7432 OR: pin names not known; wires that end beside it: Bus[7], Bus[5], OR_p3, OR_p4, OR_p5, OR_p6, Bus[6], Bus[4], OR_p6, Bus[3], OR_p4
  // DIP_7404 NOT: pin names not known; wires that end beside it: OR_p3, OR_p5, NOT_p3
  // DIP_74151 MUX_8_in: pin names not known; wires that end beside it: 1'b0, 1'b0, 1'b0, Accu[7], MUX_8_in_p5, 1'b0, 1'b0, 1'b0, 1'b0, 1'b0, Bus[0], Bus[1], Bus[2]
  // DIP_7408 AND: pin names not known; wires that end beside it: NOT_p3, NOT_p3, AND_p3, MUX_8_in_p5, Output_Acc[3], Output_Acc[7], NOT_p3, NOT_p3, AND_p9
  // DIP_74151 MUX_8_in_2: pin names not known; wires that end beside it: 1'b0, 1'b0, Accu[7], Accu[6], MUX_8_in_2_p5, 1'b0, 1'b0, 1'b0, 1'b0, 1'b0, Bus[0], Bus[1], Bus[2]
  // DIP_7408 AND_2: pin names not known; wires that end beside it: MUX_8_in_2_p5, Output_Acc[2], Output_Acc[6], NOT_p3, NOT_p3, AND_2_p6, AND_2_p7, Output_Acc[1], Output_Acc[5], NOT_p3, NOT_p3, AND_2_p12, AND_2_p13, Output_Acc[0], Output_Acc[4]
  // DIP_74151 MUX_8_in_3: pin names not known; wires that end beside it: 1'b0, Accu[7], Accu[6], Accu[5], AND_2_p7, 1'b0, 1'b0, 1'b0, 1'b0, 1'b0, Bus[0], Bus[1], Bus[2]
  // DIP_74151 MUX_8_in_4: pin names not known; wires that end beside it: Accu[7], Accu[6], Accu[5], Accu[4], AND_2_p13, 1'b0, 1'b0, 1'b0, 1'b0, 1'b0, Bus[0], Bus[1], Bus[2]
  // DIP_74151 MUX_8_in_5: pin names not known; wires that end beside it: Accu[6], Accu[5], Accu[4], Accu[3], AND_p3, 1'b0, Accu[7], 1'b0, 1'b0, 1'b0, Bus[0], Bus[1], Bus[2]
  // DIP_74151 MUX_8_in_6: pin names not known; wires that end beside it: Accu[5], Accu[4], Accu[3], Accu[2], AND_p9, 1'b0, Accu[6], Accu[7], 1'b0, 1'b0, Bus[0], Bus[1], Bus[2]
  // DIP_74151 MUX_8_in_7: pin names not known; wires that end beside it: Accu[4], Accu[3], Accu[2], Accu[1], AND_2_p6, 1'b0, Accu[5], Accu[6], Accu[7], 1'b0, Bus[0], Bus[1], Bus[2]
  // DIP_74151 MUX_8_in_8: pin names not known; wires that end beside it: Accu[3], Accu[2], Accu[1], Accu[0], AND_2_p12, 1'b0, Accu[4], Accu[5], Accu[6], Accu[7], Bus[0], Bus[1], Bus[2]
endmodule

module INV74 (
  input  [7:0] Input,
  output [7:0] Output
);

  // DIP_7404 INV: pin names not known; wires that end beside it: Input[5], Input[2], Output[5], Output[2], Input[4], Input[1], Output[4], Output[1], Input[3], Input[0], Output[3]
  // DIP_7404 INV_2: pin names not known; wires that end beside it: Output[0], Input[6], Output[6], Input[7], Output[7]

  // Notes on the sheet:
  //   Maby combine with shift right/left
endmodule

module CMPZERO74 (
  input  [7:0] Input,
  input  is_zero
);

  wire OR_2_p1, OR_2_p2, OR_2_p7, OR_2_p8, OR_p3, OR_p4, OR_p5;

  // DIP_7432 OR: pin names not known; wires that end beside it: Input[5], Input[4], OR_p3, OR_p4, OR_p5, OR_p3, OR_p5, Input[3], Input[6]
  // DIP_7432 OR_2: pin names not known; wires that end beside it: OR_2_p1, OR_2_p2, OR_p4, OR_2_p2, Input[2], Input[7], OR_2_p7, OR_2_p8, OR_2_p1, Input[1]
  // DIP_7404 NOT: pin names not known; wires that end beside it: Input[0], OR_2_p7, OR_2_p8, is_zero
endmodule

module MUX (
  input  [7:0] AND,
  input  [3:0] CU,
  input  [7:0] OR,
  input  [7:0] XOR,
  input  [7:0] ADD1,
  input  [7:0] ADD2,
  input  [7:0] ADD3,
  input  [7:0] ZERO1,
  input  [7:0] ZERO2,
  input  [7:0] SHL1,
  input  [7:0] SHL2,
  input  [7:0] SHR1,
  input  [7:0] SHR2,
  input  [7:0] ACCU1,
  input  [7:0] ACCU2,
  input  [7:0] INV1,
  input  [7:0] INV2,
  output [7:0] Output_Accu
);

  Mux2bit MUX_Modul (
    ._16_Bit_input_1({INV2[0], INV1[0], ACCU2[0], ACCU1[0], SHR2[0], SHR1[0], SHL2[0], SHL1[0], ZERO2[0], ZERO1[0], ADD3[0], ADD2[0], ADD1[0], XOR[0], OR[0], AND[0]}),
    ._16_Bit_input_2({INV2[1], INV1[1], ACCU2[1], ACCU1[1], SHR2[1], SHR1[1], SHL2[1], SHL1[1], ZERO2[1], ZERO1[1], ADD3[1], ADD2[1], ADD1[1], XOR[1], OR[1], AND[1]}),
    .Bit_2(Output_Accu[1]), .Bit_1(Output_Accu[0]), .CU(CU));
  Mux2bit MUX_Modul_2 (
    ._16_Bit_input_1({INV2[2], INV1[2], ACCU2[2], ACCU1[2], SHR2[2], SHR1[2], SHL2[2], SHL1[2], ZERO2[2], ZERO1[2], ADD3[2], ADD2[2], ADD1[2], XOR[2], OR[2], AND[2]}),
    ._16_Bit_input_2({INV2[3], INV1[3], ACCU2[3], ACCU1[3], SHR2[3], SHR1[3], SHL2[3], SHL1[3], ZERO2[3], ZERO1[3], ADD3[3], ADD2[3], ADD1[3], XOR[3], OR[3], AND[3]}),
    .Bit_2(Output_Accu[3]), .Bit_1(Output_Accu[2]), .CU(CU));
  Mux2bit MUX_Modul_3 (
    ._16_Bit_input_1({INV2[4], INV1[4], ACCU2[4], ACCU1[4], SHR2[4], SHR1[4], SHL2[4], SHL1[4], ZERO2[4], ZERO1[4], ADD3[4], ADD2[4], ADD1[4], XOR[4], OR[4], AND[4]}),
    ._16_Bit_input_2({INV2[5], INV1[5], ACCU2[5], ACCU1[5], SHR2[5], SHR1[5], SHL2[5], SHL1[5], ZERO2[5], ZERO1[5], ADD3[5], ADD2[5], ADD1[5], XOR[5], OR[5], AND[5]}),
    .Bit_2(Output_Accu[5]), .Bit_1(Output_Accu[4]), .CU(CU));
  Mux2bit MUX_Modul_4 (
    ._16_Bit_input_1({INV2[6], INV1[6], ACCU2[6], ACCU1[6], SHR2[6], SHR1[6], SHL2[6], SHL1[6], ZERO2[6], ZERO1[6], ADD3[6], ADD2[6], ADD1[6], XOR[6], OR[6], AND[6]}),
    ._16_Bit_input_2({INV2[7], INV1[7], ACCU2[7], ACCU1[7], SHR2[7], SHR1[7], SHL2[7], SHL1[7], ZERO2[7], ZERO1[7], ADD3[7], ADD2[7], ADD1[7], XOR[7], OR[7], AND[7]}),
    .Bit_2(Output_Accu[7]), .Bit_1(Output_Accu[6]), .CU(CU));
endmodule

module Mux2bit (
  input  [15:0] _16_Bit_input_1,
  input  [15:0] _16_Bit_input_2,
  input  [3:0] CU,
  output Bit_2,
  output Bit_1
);

  wire dip_74153_2_p2, dip_74153_2_p11, dip_74153_3_p1, dip_74153_3_p8, dip_74153_4_p2, dip_74153_4_p9,
       dip_74153_4_p12, dip_74153_4_p19;

  // DIP_74153 dip_74153_1: pin names not known; wires that end beside it: 1'b0, CU[1], _16_Bit_input_1[3], _16_Bit_input_1[2], _16_Bit_input_1[1], 1'b0, CU[0], _16_Bit_input_2[3], _16_Bit_input_2[2]
  // DIP_74153 dip_74153_2: pin names not known; wires that end beside it: _16_Bit_input_1[0], dip_74153_2_p2, 1'b0, CU[1], _16_Bit_input_1[7], _16_Bit_input_1[6], _16_Bit_input_1[5], _16_Bit_input_1[4], _16_Bit_input_2[1], _16_Bit_input_2[0], dip_74153_2_p11, 1'b0, CU[0], _16_Bit_input_2[7], _16_Bit_input_2[6], _16_Bit_input_2[5]
  // DIP_74153 dip_74153_3: pin names not known; wires that end beside it: dip_74153_3_p1, 1'b0, CU[1], _16_Bit_input_1[11], _16_Bit_input_1[10], _16_Bit_input_1[9], _16_Bit_input_2[4], dip_74153_3_p8, 1'b0, CU[0], _16_Bit_input_2[11], _16_Bit_input_2[10]
  // DIP_74153 dip_74153_4: pin names not known; wires that end beside it: _16_Bit_input_1[8], dip_74153_4_p2, 1'b0, CU[1], _16_Bit_input_1[15], _16_Bit_input_1[14], _16_Bit_input_1[13], _16_Bit_input_1[12], dip_74153_4_p9, _16_Bit_input_2[9], _16_Bit_input_2[8], dip_74153_4_p12, 1'b0, CU[0], _16_Bit_input_2[15], _16_Bit_input_2[14], _16_Bit_input_2[13], _16_Bit_input_2[12], dip_74153_4_p19
  // DIP_74153 dip_74153_5: pin names not known; wires that end beside it: 1'b0, CU[2], dip_74153_4_p9, dip_74153_4_p2, dip_74153_3_p1, dip_74153_2_p2, Bit_1, 1'b0, CU[3], dip_74153_4_p19, dip_74153_4_p12, dip_74153_3_p8, dip_74153_2_p11, Bit_2
endmodule

module test (
  input  [1:0] in_1,
  input  [7:0] in_2
);

  wire dip_74153_1_p13, dip_74153_1_p14;

  // DIP_74153 dip_74153_1: pin names not known; wires that end beside it: 1'b0, 1'b0, in_1[1], in_1[0], in_2[3], in_2[7], in_2[2], in_2[6], in_2[1], in_2[5], in_2[0], in_2[4], dip_74153_1_p13, dip_74153_1_p14
endmodule
